# Fritzing sketch MPU6050_TEENSY (saved by Fritzing 0.9.9b)
breadboards: 1

parts:
  Teensy1 = Teensy 4.1
  MPU-1 = Adafruit MPU6050

nets:
  N1: Teensy1.GND, Teensy1.GND2#55
  N2: Teensy1.A4/D18, MPU-1.SDA
  N3: Teensy1.A5/D19, MPU-1.SCL
  N4: Teensy1.3V3_LOW, MPU-1.VCC
  N5: Teensy1.GND2#31, MPU-1.GND

notes:
  Teensy is 3V logic level, connect mpu6050 Vin pin to 3V pin!
  Connect IMU to I2C pins on the Teensy as shown in pinout,
  SCL =19 SDA=18

custom parts:
  Teensy 4.1: The Teensy is a complete USB-based microcontoller development system, in a very small footprint, capable of implementing many types of projects. All programming is done via the USB port. No special programmer is needed, only a standard micro-USB cable and a PC or Macintosh with a USB port.
  Adafruit MPU6050: The MPU-6050 is a popular six axis accelerometer and gyroscope (gyro) that has all the info you need on how things are shakin' and spinnin' . With six axes of sensing and 16-bit measurements, you'll have everything you need to give your robot friend an inner ear. This combination of gyroscopes and accelerometers is commonly referred to as an Inertial Measurement Unit or IMU. Not so long ago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
